# Fritzing sketch controller (saved by Fritzing 0.9.4)
circuit board: 8.46667cm x 5.64444cm
breadboards: 1

parts:
  Uno_R3 = Arduino Uno (Rev3)
  joy1 = Thumb Joystick
  joy2 = Thumb Joystick
  headlightButton = Pushbutton [package="[THT]"]
  hornButton = Pushbutton [package="[THT]"]

nets:
  N1: Uno_R3.A0, joy1.VERT
  N2: Uno_R3.A1, joy1.HORZ
  N3: Uno_R3.A2, joy2.VERT
  N4: Uno_R3.A3, joy2.HORZ
  N5: Uno_R3.D2, hornButton.Pin_3, hornButton.Pin_4
  N6: Uno_R3.D3_PWM, headlightButton.Pin_1, headlightButton.Pin_2
  VCC: Uno_R3.5V, joy1.VCC, joy2.VCC
  GND: Uno_R3.GND, joy1.GND, joy2.GND, headlightButton.Pin_3, headlightButton.Pin_4, hornButton.Pin_1, hornButton.Pin_2
