# Fritzing sketch rc_car_bt (saved by Fritzing 0.9.4)
circuit board: 8.46667cm x 5.64444cm
breadboards: 1

parts:
  220R = Resistor [tolerance=±5% resistance=220 package=THT]
  220R_2 = Resistor [tolerance=±5% resistance=220 package=THT]
  220R_3 = Resistor [tolerance=±5% resistance=220 package=THT]
  220R_4 = Resistor [tolerance=±5% resistance=220 package=THT]
  horn_piezo = Piezo Speaker
  steering_servo = Basic Servo
  tailight_LED = LED - 5mm [color="Red (633nm)" package="5 mm [THT]"]
  tailight_LED_2 = LED - 5mm [color="Red (633nm)" package="5 mm [THT]"]
  headlight_LED = LED - 5mm [color="White (6500K)" package="5 mm [THT]"]
  headlight_LED_2 = LED - 5mm [color="White (6500K)" package="5 mm [THT]"]
  Part2 = Bluetooth HC-05 Macho
  IC1 = L293D [package=THT]
  Part1 = Arduino Nano (Rev3.0)
  M1 = DC Motor
  BAT2 = BC9VPC [package=bc9vpc]
  U1 = LIPO-2000mAh [package=lipo-2000]

nets:
  N1: 220R.Pin_0, 220R_3.Pin_0, Part1.D6
  N2: 220R.Pin_1, tailight_LED.anode
  N3: 220R_2.Pin_0, headlight_LED.anode
  N4: 220R_2.Pin_1, 220R_4.Pin_1, Part1.D8
  N5: 220R_3.Pin_1, tailight_LED_2.anode
  N6: 220R_4.Pin_0, headlight_LED_2.anode
  GND: horn_piezo.pin1, steering_servo.gnd, tailight_LED.cathode, tailight_LED_2.cathode, headlight_LED.cathode, headlight_LED_2.cathode, Part2.GND, IC1.0V, Part1.GND, BAT2.V-, U1.-
  N7: horn_piezo.pin2, Part1.D10
  N8: steering_servo.vcc, IC1.+V, U1.+
  N9: steering_servo.pulse, Part1.D7
  N10: Part2.TXD, Part1.D4
  N11: Part2.RXD, Part1.D3
  VCC: Part2.VCC, IC1.+Vmotor, Part1.5V
  N12: IC1.Enable_1, Part1.D5
  N13: IC1.In_1, Part1.D12/MISO
  N14: IC1.Out_1_(_Controlled_by_Enable_1_), IC1.Out_2_(_Controlled_by_Enable_1_), M1.pin_1, M1.pin_2
  N15: IC1.In_2, Part1.D11/MOSI
  N16: Part1.VIN, BAT2.V+
