# Fritzing sketch rc_car_proto (saved by Fritzing 0.9.4)
breadboards: 2

parts:
  Uno_R3 = Arduino Uno (Rev3)
  joy1 = Thumb Joystick
  joy2 = Thumb Joystick
  headlightButton = Pushbutton [package="[THT]"]
  hornButton = Pushbutton [package="[THT]"]
  220R = Resistor [tolerance=±5% resistance=220 package=THT]
  220R_2 = Resistor [tolerance=±5% resistance=220 package=THT]
  220R_3 = Resistor [tolerance=±5% resistance=220 package=THT]
  220R_4 = Resistor [tolerance=±5% resistance=220 package=THT]
  horn_piezo = Piezo Speaker
  M1 = DC Motor
  steering_servo = Basic Servo
  tailight_LED = LED - 5mm [color="Red (633nm)" package="5 mm [THT]"]
  tailight_LED_2 = LED - 5mm [color="Red (633nm)" package="5 mm [THT]"]
  headlight_LED = LED - 5mm [color="White (6500K)" package="5 mm [THT]"]
  headlight_LED_2 = LED - 5mm [color="White (6500K)" package="5 mm [THT]"]
  IC1 = L293D [package=THT]
  BAT1 = BC9VPC [package=bc9vpc]

nets:
  N1: Uno_R3.A0, joy1.VERT
  N2: Uno_R3.A1, joy1.HORZ
  N3: Uno_R3.A2, joy2.VERT
  N4: Uno_R3.A3, joy2.HORZ
  N5: Uno_R3.D8, 220R_2.Pin_1, 220R_4.Pin_1
  N6: Uno_R3.D11_PWM/MOSI, horn_piezo.pin2
  N7: Uno_R3.D12/MISO, IC1.In_2
  N8: Uno_R3.D13/SCK, IC1.In_1
  N9: Uno_R3.D2, hornButton.Pin_3, hornButton.Pin_4
  N10: Uno_R3.D3_PWM, headlightButton.Pin_1, headlightButton.Pin_2
  N11: Uno_R3.D5_PWM, IC1.Enable_1
  N12: Uno_R3.D6_PWM, 220R.Pin_0, 220R_3.Pin_0
  N13: Uno_R3.D7, steering_servo.pulse
  VCC: Uno_R3.5V, joy1.VCC, joy2.VCC, IC1.+Vmotor
  GND: Uno_R3.GND, joy1.GND, joy2.GND, headlightButton.Pin_3, headlightButton.Pin_4, hornButton.Pin_1, hornButton.Pin_2, horn_piezo.pin1, steering_servo.gnd, tailight_LED.cathode, tailight_LED_2.cathode, headlight_LED.cathode, headlight_LED_2.cathode, IC1.0V, BAT1.V-
  N14: 220R.Pin_1, tailight_LED.anode
  N15: 220R_2.Pin_0, headlight_LED.anode
  N16: 220R_3.Pin_1, tailight_LED_2.anode
  N17: 220R_4.Pin_0, headlight_LED_2.anode
  N18: M1.pin_1, IC1.Out_1_(_Controlled_by_Enable_1_)
  N19: M1.pin_2, IC1.Out_2_(_Controlled_by_Enable_1_)
  N20: steering_servo.vcc, IC1.+V, BAT1.V+
